# Fritzing sketch circuit (saved by Fritzing 0.9.3b)
breadboards: 1

parts:
  Part1 = Adafruit DRV8833 DC/Stepper Motor Driver [part_number="Adafruit #3297"]
  Part2 = Adafruit DRV8833 DC/Stepper Motor Driver [part_number="Adafruit #3297"]
  Q1 = NPN-Transistor [package="TO92 [THT]"]
  M1 = DC Motor
  R1 = Resistor [tolerance=±5% resistance=220 package=THT]
  D1 = Rectifier Diode [part_number=1N4001 package="300 mil [THT]"]
  Part3 = Arduino Uno (Rev3)
  VCC1 = Battery
  VCC2 = Battery
  VCC3 = Battery
  M2 = Stepper Motor - Bipolar
  M3 = Stepper Motor - Bipolar
  J1 = Basic Servo
  J2 = Basic Servo

nets:
  VCC: Part1.PWRIN, Part2.PWRIN, M1.pin_1, D1.cathode, J1.vcc, J2.vcc
  GND: Part1.GND, Part2.GND, Q1.E, Part3.GND, J1.gnd, J2.gnd
  N1: Part1.AOUT2, M2.C
  N2: Part1.AOUT1, M2.A
  N3: Part1.BOUT1, M2.D
  N4: Part1.BOUT2, M2.B
  N5: Part1.BIN2, Part3.D4
  N6: Part1.!SLEEP, Part2.!SLEEP, Part3.5V
  N7: Part1.AIN2, Part3.D3_PWM
  N8: Part1.AIN1, Part3.D2
  N9: Part2.AOUT2, Part3.D10_PWM/SS, M3.C
  N10: Part2.BIN1, Part3.D8
  N11: Part2.BIN2, Part3.D9_PWM
  N12: Part2.AIN2, Part3.D7
  N13: Part2.AIN1, Part3.D6_PWM
  N14: Q1.B, M1.pin_2, D1.anode
  N15: Q1.C, R1.Pin_1
  N16: R1.Pin_0, Part3.D11_PWM/MOSI
  N17: Part3.A4/SDA, J1.pulse
  N18: Part3.A5/SCL, J2.pulse
  N19: Part3.VIN, VCC1.+
  N20: VCC1.-, VCC3.+
  N21: VCC2.+, VCC3.-

custom parts:
  Adafruit DRV8833 DC/Stepper Motor Driver: Spin two DC motors or step one bi-polar or uni-polar stepper with up to 1.2A per channel using the DRV8833. This motor driver chip is a nice alternative to the TB6612 driver. Like that chip, you get 2 full H-bridges, but this chip is better for low voltage uses (can run from 2.7V up to 10.8V motor power) and has built in current limiting capability. We set it up for 1A current limiting so you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
